# Fritzing sketch circuit_diagram (saved by Fritzing 1.0.1rc)

parts:
  R1 = Resistor [tolerance=±5% power=0.25W resistance=10k package=THT]
  Sensor_2 = Sparkfun sen18642
  Sensor_1 = Sparkfun sen18642
  Click_button = Pushbutton [package="[THT]"]
  LiPo_cell = Lithium Ion Polymer Battery 3.7v 2500mAh [part_number=328]
  LiPo_Charger = Adafruit BQ24074 Solar-DC-USB Lipo Charger
  5V_Step-up = Pololu 5V Step-Up Regulator
  Toggle_switch = Toggle Switch [package=THT]
  C3 = Electrolytic Capacitor [capacitance=33µF voltage=35V package="0405 [SMD, electrolytic]"]
  MCU = Arduino Nano 33 BLE Sense

nets:
  GND: R1.Pin_0, Sensor_2.Pin_5, Sensor_1.Pin_5, Sensor_1.Pin_11, LiPo_cell.negative, LiPo_Charger.GND, 5V_Step-up.GND, C3.-, MCU.GND, MCU.A7
  N1: R1.Pin_1, Click_button.Pin_3, Click_button.Pin_4, MCU.D2
  N2: Sensor_2.Pin_6, Sensor_2.Pin_12, Sensor_1.Pin_6, Sensor_1.Pin_12, Click_button.Pin_1, Click_button.Pin_2, MCU.3V3
  N3: Sensor_2.Pin_7, Sensor_1.Pin_7, MCU.A4
  N4: Sensor_2.Pin_8, Sensor_1.Pin_8, MCU.A5
  N5: Sensor_2.Pin_15, MCU.D4
  N6: Sensor_1.Pin_15, MCU.D3~
  N7: LiPo_cell.positive, LiPo_Charger.VLIPO
  N8: LiPo_Charger.OUT, Toggle_switch.COM
  N9: 5V_Step-up.VIN, Toggle_switch.L1, C3.+
  N10: 5V_Step-up.VOUT, MCU.VIN

custom parts:
  Sparkfun sen18642: The SparkFun Qwiic ToF Imager is built around VL53L5CX from ST Electronics; a state of the art, Time-of-Flight (ToF), multizone ranging sensor.
  Lithium Ion Polymer Battery 3.7v 2500mAh: Lithium ion polymer (also known as 'lipo' or 'lipoly') batteries are thin, light and powerful. The output ranges from 4.2V when completely charged to 3.7V. This battery has a capacity of 2500mAh for a total of about 10 Wh. The batteries come pre-attached with a genuine 2-pin JST-PH connector as shown and include the necessary protection circuitry.
  Arduino Nano 33 BLE Sense: The Nano 33 BLE Sense (without headers) is Arduino’s 3.3V AI enabled board in the smallest available form factor: 45x18mm! The Arduino Nano 33 BLE Sense is a completely new board on a well-known form factor. It comes with a series of embedded sensors: 9 axis inertial sensor: what makes this board ideal for wearable devices humidity, and temperature sensor: to get highly accurate measurements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
